// Digital circuit Adder-Subtractor-ModernEquiv-ICLogicFinal (10-17).dig as structural Verilog
module Adder_Subtractor_ModernEquiv_ICLogicFinal__10_17 (
  input  X,
  input  Y,
  input  Cin,
  input  \Ā_S ,
  output Sum,
  output Cout
);

  wire multiplexer_1_out, multiplexer_2_out, nand_1_out, nand_2_out, nand_3_out, nand_4_out, nand_6_out,
       nand_7_out, nor_1_out, nor_2_out, nor_3_out, nor_4_out, not_1_out, not_2_out, not_3_out, not_4_out,
       not_5_out;

  not not_1 (not_1_out, X);
  not not_2 (not_2_out, Y);
  not not_3 (not_3_out, Cin);
  not not_4 (not_4_out, not_1_out);
  nand nand_1 (nand_1_out, not_2_out, not_3_out);
  nor nor_1 (nor_1_out, not_2_out, not_3_out);
  not not_5 (not_5_out, nor_1_out);
  nand nand_2 (nand_2_out, not_1_out, nand_1_out, not_5_out);
  nand nand_3 (nand_3_out, not_4_out, nand_1_out, not_5_out);
  nand nand_4 (nand_4_out, not_4_out, nand_3_out);
  nand nand_5 (Sum, nand_2_out, nand_4_out);
  nor nor_2 (nor_2_out, nand_2_out, not_5_out);
  nand nand_6 (nand_6_out, nand_2_out, not_5_out);
  nand nand_7 (nand_7_out, nand_3_out, not_5_out);
  nor nor_3 (nor_3_out, nand_3_out, not_5_out);
  Multiplexer multiplexer_1 (.sel(\Ā_S ), .in_0(nor_2_out), .in_1(nand_6_out), .out(multiplexer_1_out));
  Multiplexer multiplexer_2 (.sel(\Ā_S ), .in_0(nand_7_out), .in_1(nor_3_out), .out(multiplexer_2_out));
  nor nor_4 (nor_4_out, multiplexer_1_out, multiplexer_2_out);
  not not_6 (Cout, nor_4_out);

  // Notes on the sheet:
  //   Borrow
  //   Carry
endmodule
