// Digital circuit Base-Converter.dig as structural Verilog
module Base_Converter (
  input  clk,
  input  D0,
  input  set,
  input  clr,
  input  clk_2,
  input  D1,
  input  clk_3,
  input  D2,
  input  clk_4,
  input  D3,
  output Q3,
  output Q2,
  output Q1,
  output Q0,
  output Q7,
  output Q6,
  output Q5,
  output Q4,
  output Q11,
  output Q10,
  output Q9,
  output Q8,
  output Q15,
  output Q14,
  output Q13,
  output Q12
);

  D_FF_AS _15 (.Set(set), .D(D3), .C(clk_4), .Clr(clr), .Q(Q15));  // open: nQ
  D_FF_AS _11 (.Set(set), .D(D2), .C(clk_3), .Clr(clr), .Q(Q11));  // open: nQ
  D_FF_AS _7 (.Set(set), .D(D1), .C(clk_2), .Clr(clr), .Q(Q7));  // open: nQ
  D_FF_AS _3 (.Set(set), .D(D0), .C(clk), .Clr(clr), .Q(Q3));  // open: nQ
  D_FF_AS _14 (.Set(set), .D(Q15), .C(clk_4), .Clr(clr), .Q(Q14));  // open: nQ
  D_FF_AS _10 (.Set(set), .D(Q11), .C(clk_3), .Clr(clr), .Q(Q10));  // open: nQ
  D_FF_AS _6 (.Set(set), .D(Q7), .C(clk_2), .Clr(clr), .Q(Q6));  // open: nQ
  D_FF_AS _2 (.Set(set), .D(Q3), .C(clk), .Clr(clr), .Q(Q2));  // open: nQ
  D_FF_AS _13 (.Set(set), .D(Q14), .C(clk_4), .Clr(clr), .Q(Q13));  // open: nQ
  D_FF_AS _9 (.Set(set), .D(Q10), .C(clk_3), .Clr(clr), .Q(Q9));  // open: nQ
  D_FF_AS _5 (.Set(set), .D(Q6), .C(clk_2), .Clr(clr), .Q(Q5));  // open: nQ
  D_FF_AS _1 (.Set(set), .D(Q2), .C(clk), .Clr(clr), .Q(Q1));  // open: nQ
  D_FF_AS _12 (.Set(set), .D(Q13), .C(clk_4), .Clr(clr), .Q(Q12));  // open: nQ
  D_FF_AS _8 (.Set(set), .D(Q9), .C(clk_3), .Clr(clr), .Q(Q8));  // open: nQ
  D_FF_AS _4 (.Set(set), .D(Q5), .C(clk_2), .Clr(clr), .Q(Q4));  // open: nQ
  D_FF_AS _0 (.Set(set), .D(Q1), .C(clk), .Clr(clr), .Q(Q0));  // open: nQ
endmodule
